// Logisim project full_design.circ as structural Verilog: 4 circuits, main circuit main
module main (
  output out_1,
  output out_2,
  output [2:0] out_3,
  output [15:0] out_4,
  output [15:0] out_5,
  output [15:0] out_6,
  output [15:0] out_7,
  output [15:0] out_8,
  output [15:0] out_9,
  output [15:0] out_10,
  output [15:0] out_11,
  output [1:0] out_12,
  output [15:0] out_13
);

  wire ALUsrc, and_1_out, and_2_out, and_3_out, and_4_out, and_5_out, and_6_out, and_7_out, and_8_out, Clock,
       instRead, JAEsignal, JAsignal, JBEsignal, JBsignal, JEsignal, JUMPsignal, memRead, memWrite,
       not_1_out, not_2_out, not_3_out, not_4_out, not_5_out, not_6_out, or_1_out, or_2_out, or_3_out,
       PCread, PCselect, regWrite;
  wire [2:0] adrBits, multiplexer_3_out, regDest, RegSrc1, RegSrc2;
  wire [3:0] opcode;
  wire [9:0] bit_extender_3_out;
  wire [15:0] adder_1_out, adder_2_out, alu_1_result_of_operation, bit_extender_1_out, bit_extender_2_out,
       currentPC, multiplexer_1_out, multiplexer_2_out, multiplexer_4_out, multiplexer_5_out,
       register_file_1_register_2_data, rom_1_data, src1Data;

  Clock clock_1 (.out(Clock));
  Multiplexer #(.width(16), .enable("false")) multiplexer_1 (
    .in0(adder_1_out), .in1(multiplexer_2_out), .out(multiplexer_1_out), .sel(PCselect));
  Control_Unit control_unit_1 (
    .opcode(opcode), .state_value(out_3), .PCread(PCread), .instRead(instRead), .ALUsrc(ALUsrc),
    .regWrite(regWrite), .clock(Clock), .PCSelect(PCselect), .JEsignal(JEsignal), .JAsignal(JAsignal),
    .JBsignal(JBsignal), .JAEsignal(JAEsignal), .JBEsignal(JBEsignal), .JUMP(JUMPsignal), .memRead(memRead),
    .ALUcontrol(out_12), .memWrite(memWrite));
  Register #(.width(16)) PC (.D(multiplexer_1_out), .en(or_1_out), .Q(currentPC), .clk(Clock));  // open: clr
  or or_1 (or_1_out, PCselect, PCread);
  Adder #(.width(16)) adder_1 (.a(16'h1), .b(currentPC), .out(adder_1_out));  // open: cin, cout
  Multiplexer #(.width(16), .enable("false")) multiplexer_2 (
    .in0(adder_2_out), .in1(currentPC), .out(multiplexer_2_out), .sel(not_1_out));
  not not_1 (not_1_out, or_2_out);
  ROM #(.addrWidth(16), .dataWidth(16)) rom_1 (.addr(currentPC), .data(rom_1_data), .sel(instRead));
  Adder #(.width(16)) adder_2 (.a(currentPC), .b(bit_extender_1_out), .out(adder_2_out));  // open: cin, cout
  Register #(.width(16)) CurrentInst (
    .D(rom_1_data), .Q({opcode, regDest, RegSrc1, adrBits, RegSrc2}), .clk(Clock));  // open: en, clr
  assign bit_extender_1_out = {{4{regDest[2]}}, {regDest, RegSrc1, adrBits, RegSrc2}};  // Bit_Extender bit_extender_1
  or or_2 (or_2_out, and_1_out, and_3_out, and_5_out, and_7_out, and_8_out, JUMPsignal);
  Multiplexer #(.width(3), .enable("false")) multiplexer_3 (
    .in0(RegSrc1), .in1(regDest), .out(multiplexer_3_out), .sel(memWrite));
  and and_1 (and_1_out, JEsignal, and_2_out);
  and and_2 (and_2_out, out_1, not_3_out);
  and and_3 (and_3_out, JAsignal, and_4_out);
  and and_4 (and_4_out, not_4_out, not_5_out);
  and and_5 (and_5_out, JBsignal, and_6_out);
  and and_6 (and_6_out, not_6_out, out_2);
  and and_7 (and_7_out, JAEsignal, not_2_out);
  not not_2 (not_2_out, out_2);
  and and_8 (and_8_out, JBEsignal, or_3_out);
  or or_3 (or_3_out, out_1, out_2);
  Register_File register_file_1 (
    .write_data(multiplexer_4_out), .register_1_data(src1Data),
    .register_2_data(register_file_1_register_2_data), .write_source__register(regDest),
    .write_enable(regWrite), .Clock(Clock), .read_register1(multiplexer_3_out), .read_register_2(RegSrc2),
    .reg0(out_4), .reg1(out_5), .reg2(out_6), .reg3(out_7), .reg4(out_8), .reg5(out_9), .reg7(out_11),
    .reg6(out_10));
  not not_3 (not_3_out, out_2);
  not not_4 (not_4_out, out_1);
  not not_5 (not_5_out, out_2);
  not not_6 (not_6_out, out_1);
  Multiplexer #(.width(16), .enable("false")) multiplexer_4 (
    .in0(alu_1_result_of_operation), .in1(out_13), .out(multiplexer_4_out), .sel(memRead));
  assign bit_extender_2_out = {{10{adrBits[2]}}, {adrBits, RegSrc2}};  // Bit_Extender bit_extender_2
  Multiplexer #(.width(16), .enable("false")) multiplexer_5 (
    .in0(register_file_1_register_2_data), .in1(bit_extender_2_out), .out(multiplexer_5_out), .sel(ALUsrc));
  ALU alu_1 (
    .Data_input_1(src1Data), .Data_input_2(multiplexer_5_out),
    .Result_of_operation(alu_1_result_of_operation), .zeroFlag(out_1), .clock(Clock), .ALUcontrol(out_12),
    .carryFlag(out_2));
  assign bit_extender_3_out = {{1{1'b0}}, {RegSrc1, adrBits, RegSrc2}};  // Bit_Extender bit_extender_3
  RAM #(.addrWidth(10), .dataWidth(16), .bus("separate")) ram_1 (
    .addr(bit_extender_3_out), .din(src1Data), .data(out_13), .str(memWrite), .clk(Clock), .ld(memRead));  // open: sel, clr

  // Other names for the same wires on the sheet: ALUcontrol[1:0] = out_12; CF = out_2; reg0[15:0] = out_4;
  //   reg1[15:0] = out_5; reg2[15:0] = out_6; reg3[15:0] = out_7; reg4[15:0] = out_8; reg5[15:0] = out_9;
  //   reg6[15:0] = out_10; reg7[15:0] = out_11; ZF = out_1

  // Notes on the sheet:
  //   contents of rom_1 (hex, n*v repeats v):
  //   a000 1003 123e 2401 601 38c7 b004 aa04 4040 6003 7003 482 482 482 cffb
endmodule

module Control_Unit (
  input  clock,
  input  [3:0] opcode,
  output [2:0] state_value,
  output PCread,
  output instRead,
  output memRead,
  output ALUsrc,
  output regWrite,
  output PCSelect,
  output memWrite,
  output JEsignal,
  output [1:0] ALUcontrol,
  output JAsignal,
  output JBsignal,
  output JAEsignal,
  output JBEsignal,
  output JUMP
);

  wire ADD, ADDI, AND, and_12_out, and_16_out, ANDI, CMP, JA, JAE, JB, JBE, JE, JUMP_t, LD, memRead1,
       memRead2, or_1_out, or_2_out, or_3_out, or_4_out, resetState, resetState1, resetState2, ST, State_3,
       State_4, State_5;

  Counter #(.width(3), .max('h7)) counter_1 (
    .Q(state_value), .clk(clock), .clr(resetState));  // open: load, D, count, carry
  Decoder #(.select(4), .enable("false")) decoder_1 (
    .out0(ADD), .out1(ADDI), .out2(AND), .out3(ANDI), .out4(CMP), .out5(JE), .out6(JA), .out7(JB),
    .out8(JBE), .out9(JAE), .out10(LD), .out11(ST), .out12(JUMP_t), .sel(opcode));  // open: out13, out14, out15
  Decoder #(.select(3), .enable("false")) decoder_2 (
    .out0(PCread), .out1(instRead), .out2(State_3), .out3(State_4), .out4(State_5), .sel(state_value));  // open: out5, out6, out7
  and and_1 (ALUsrc, State_3, or_1_out);
  and and_2 (ALUcontrol[1], State_3, CMP);
  and and_3 (ALUcontrol[0], State_3, or_2_out);
  or or_1 (or_1_out, ADDI, ANDI);
  or or_2 (or_2_out, AND, ANDI);
  and and_4 (memWrite, State_3, ST);
  or or_3 (or_3_out, JE, JA, JB, JAE, JBE, JUMP_t);
  and and_5 (JEsignal, State_3, JE);
  and and_6 (JAsignal, State_3, JA);
  and and_7 (JBsignal, State_3, JB);
  and and_8 (JAEsignal, State_3, JAE);
  and and_9 (JBEsignal, State_3, JBE);
  and and_10 (JUMP, State_3, JUMP_t);
  and and_11 (PCSelect, State_3, or_3_out);
  and and_12 (and_12_out, State_4, LD);
  and and_13 (memRead1, State_3, LD);
  and and_14 (memRead2, State_4, LD);
  and and_15 (resetState2, State_5, LD);
  and and_16 (and_16_out, State_3, or_4_out);
  or or_4 (or_4_out, ADDI, ADD, AND, ANDI);
  or or_5 (regWrite, and_12_out, and_16_out);
  or or_6 (memRead, memRead1, memRead2);
  or or_7 (resetState, resetState1, resetState2);
  and and_17 (resetState1, State_4, ~LD);  // AND_Gate

  // Other names for the same wires on the sheet: State_1 = PCread; State_2 = instRead
endmodule

module ALU (
  input  [1:0] ALUcontrol,
  input  [15:0] Data_input_1,
  input  [15:0] Data_input_2,
  input  clock,
  output [15:0] Result_of_operation,
  output zeroFlag,
  output carryFlag
);

  wire comparator_1_eq, comparator_1_lt;
  wire [15:0] adder_1_out, and_1_out;

  Comparator #(.width(16)) comparator_1 (
    .a(Data_input_1), .b(Data_input_2), .eq(comparator_1_eq), .lt(comparator_1_lt));  // open: gt
  Adder #(.width(16)) adder_1 (.a(Data_input_1), .b(Data_input_2), .out(adder_1_out));  // open: cin, cout
  assign and_1_out = Data_input_1 & Data_input_2;  // AND_Gate and_1, 16 bits wide
  Multiplexer #(.width(16), .enable("false")) multiplexer_1 (
    .in0(adder_1_out), .in1(and_1_out), .out(Result_of_operation), .sel(ALUcontrol[0]));
  Register #(.width(1)) zeroReg (.D(comparator_1_eq), .en(ALUcontrol[1]), .Q(zeroFlag), .clk(clock));  // open: clr
  Register #(.width(1)) u_carryFlag (.D(comparator_1_lt), .en(ALUcontrol[1]), .Q(carryFlag), .clk(clock));  // open: clr
endmodule

module Register_File (
  input  [2:0] read_register1,
  input  [2:0] write_source__register,
  input  [2:0] read_register_2,
  input  [15:0] write_data,
  input  Clock,
  input  write_enable,
  output [15:0] reg0,
  output [15:0] reg1,
  output [15:0] reg2,
  output [15:0] reg3,
  output [15:0] reg4,
  output [15:0] reg5,
  output [15:0] register_1_data,
  output [15:0] register_2_data,
  output [15:0] reg7,
  output [15:0] reg6
);

  wire and_1_out, and_2_out, and_3_out, and_4_out, and_5_out, and_6_out, and_7_out, and_8_out,
       decoder_1_out0, decoder_1_out1, decoder_1_out2, decoder_1_out3, decoder_1_out4, decoder_1_out5,
       decoder_1_out6, decoder_1_out7;

  Decoder #(.select(3), .enable("false")) decoder_1 (
    .out0(decoder_1_out0), .out1(decoder_1_out1), .out2(decoder_1_out2), .out3(decoder_1_out3),
    .out4(decoder_1_out4), .out5(decoder_1_out5), .out6(decoder_1_out6), .out7(decoder_1_out7),
    .sel(write_source__register));
  and and_1 (and_1_out, decoder_1_out0, write_enable);
  and and_2 (and_2_out, decoder_1_out1, write_enable);
  and and_3 (and_3_out, decoder_1_out2, write_enable);
  and and_4 (and_4_out, decoder_1_out3, write_enable);
  and and_5 (and_5_out, decoder_1_out4, write_enable);
  and and_6 (and_6_out, decoder_1_out5, write_enable);
  and and_7 (and_7_out, decoder_1_out6, write_enable);
  and and_8 (and_8_out, decoder_1_out7, write_enable);
  Register #(.width(16)) register_1 (.D(write_data), .en(and_1_out), .Q(reg0), .clk(Clock));  // open: clr
  Register #(.width(16)) register_2 (.D(write_data), .en(and_2_out), .Q(reg1), .clk(Clock));  // open: clr
  Register #(.width(16)) register_3 (.D(write_data), .en(and_3_out), .Q(reg2), .clk(Clock));  // open: clr
  Register #(.width(16)) register_4 (.D(write_data), .en(and_4_out), .Q(reg3), .clk(Clock));  // open: clr
  Register #(.width(16)) register_5 (.D(write_data), .en(and_5_out), .Q(reg4), .clk(Clock));  // open: clr
  Register #(.width(16)) register_6 (.D(write_data), .en(and_6_out), .Q(reg5), .clk(Clock));  // open: clr
  Register #(.width(16)) register_7 (.D(write_data), .en(and_7_out), .Q(reg6), .clk(Clock));  // open: clr
  Register #(.width(16)) register_8 (.D(write_data), .en(and_8_out), .Q(reg7), .clk(Clock));  // open: clr
  Multiplexer #(.select(3), .width(16), .enable("false")) multiplexer_1 (
    .in0(reg0), .in1(reg1), .in2(reg2), .in3(reg3), .in4(reg4), .in5(reg5), .in6(reg6), .in7(reg7),
    .out(register_1_data), .sel(read_register1));
  Multiplexer #(.select(3), .width(16), .enable("false")) multiplexer_2 (
    .in0(reg0), .in1(reg1), .in2(reg2), .in3(reg3), .in4(reg4), .in5(reg5), .in6(reg6), .in7(reg7),
    .out(register_2_data), .sel(read_register_2));
endmodule
